// Logisim project circuito-somador.circ as structural Verilog: 3 circuits, main circuit main
module main (
  input  in_1,
  input  C5,
  input  C4,
  input  C3,
  input  C3_2,
  input  C1,
  input  C0,
  input  A0,
  input  B0,
  input  A1,
  input  B1,
  input  A2,
  input  B2,
  input  A3,
  input  B3,
  input  A4,
  input  B4,
  input  A5,
  input  B5,
  output S5,
  output S4,
  output S3,
  output S2,
  output S1,
  output S0,
  output out_26
);

  wire somadorcompleto_1_out_4, somadorcompleto_1_out_5, somadorcompleto_2_out_4, somadorcompleto_2_out_5,
       somadorcompleto_3_out_4, somadorcompleto_3_out_5, somadorcompleto_4_out_4, somadorcompleto_4_out_5,
       somadorcompleto_5_out_4, somadorcompleto_5_out_5, somadorcompleto_6_out_4, somadorcompleto_6_out_5,
       somadorcompleto_7_out_5, somadorcompleto_8_out_5, somadorcompleto_9_out_5, somadorcompleto_10_out_5,
       somadorcompleto_11_out_5;

  somadorCompleto somadorcompleto_1 (
    .C(in_1), .B(A0), .A(B0), .out_4(somadorcompleto_1_out_4), .out_5(somadorcompleto_1_out_5));
  somadorCompleto somadorcompleto_2 (
    .C(somadorcompleto_1_out_5), .B(A1), .A(B1), .out_4(somadorcompleto_2_out_4),
    .out_5(somadorcompleto_2_out_5));
  somadorCompleto somadorcompleto_3 (
    .C(somadorcompleto_6_out_5), .B(A5), .A(B5), .out_4(somadorcompleto_3_out_4),
    .out_5(somadorcompleto_3_out_5));
  somadorCompleto somadorcompleto_4 (
    .C(somadorcompleto_2_out_5), .B(A2), .A(B2), .out_4(somadorcompleto_4_out_4),
    .out_5(somadorcompleto_4_out_5));
  somadorCompleto somadorcompleto_5 (
    .C(somadorcompleto_4_out_5), .B(A3), .A(B3), .out_4(somadorcompleto_5_out_4),
    .out_5(somadorcompleto_5_out_5));
  somadorCompleto somadorcompleto_6 (
    .C(somadorcompleto_5_out_5), .B(A4), .A(B4), .out_4(somadorcompleto_6_out_4),
    .out_5(somadorcompleto_6_out_5));
  somadorCompleto somadorcompleto_7 (
    .C(somadorcompleto_3_out_5), .B(somadorcompleto_1_out_4), .A(C5), .out_4(S5),
    .out_5(somadorcompleto_7_out_5));
  somadorCompleto somadorcompleto_8 (
    .C(somadorcompleto_7_out_5), .B(somadorcompleto_2_out_4), .A(C4), .out_4(S4),
    .out_5(somadorcompleto_8_out_5));
  somadorCompleto somadorcompleto_9 (
    .C(somadorcompleto_8_out_5), .B(somadorcompleto_4_out_4), .A(C3), .out_4(S3),
    .out_5(somadorcompleto_9_out_5));
  somadorCompleto somadorcompleto_10 (
    .C(somadorcompleto_9_out_5), .B(somadorcompleto_5_out_4), .A(C3_2), .out_4(S2),
    .out_5(somadorcompleto_10_out_5));
  somadorCompleto somadorcompleto_11 (
    .C(somadorcompleto_10_out_5), .B(somadorcompleto_6_out_4), .A(C1), .out_4(S1),
    .out_5(somadorcompleto_11_out_5));
  somadorCompleto somadorcompleto_12 (
    .C(somadorcompleto_11_out_5), .B(somadorcompleto_3_out_4), .A(C0), .out_4(S0), .out_5(out_26));
  Hex_Digit_Display hex_digit_display_1 (.value({S3, S2, S1, S0}));  // open: dp
endmodule

module meioSomador (
  input  in_1,
  input  in_2,
  output S,
  output CO
);

  and and_1 (CO, in_1, in_2);
  xor xor_1 (S, in_1, in_2);
endmodule

module somadorCompleto (
  input  C,
  input  B,
  input  A,
  output out_4,
  output out_5
);

  wire meiosomador_1_co, meiosomador_1_s, meiosomador_2_co;

  meioSomador meiosomador_1 (.in_1(B), .in_2(A), .S(meiosomador_1_s), .CO(meiosomador_1_co));
  meioSomador meiosomador_2 (.in_1(C), .in_2(meiosomador_1_s), .S(out_4), .CO(meiosomador_2_co));
  or or_1 (out_5, meiosomador_2_co, meiosomador_1_co);
endmodule
